# Fritzing sketch intval_3_prototype (saved by Fritzing 0.9.3b)
circuit board: 8.46667cm x 5.64444cm
breadboards: 1

parts:
  IC1 = Voltage Regulator [package=to220-igo]
  Raspberry_Pi_1 = Raspberry Pi 3 [part_number=RPI-3-V1.2]
  J5 = screw terminal, 2 pins
  J6 = screw terminal, 2 pins
  J7 = screw terminal, 2 pins
  J8 = screw terminal, 2 pins
  R1 = Resistor [tolerance=±5% resistance=330 package=THT]
  R2 = Resistor [tolerance=±5% resistance=330 package=THT]

nets:
  GND: IC1.GND, Raspberry_Pi_1.GND, J5.pin2, J6.pin2, J7.pin2
  N1: IC1.IN, J5.pin1
  N2: IC1.OUT, Raspberry_Pi_1.5V
  N3: Raspberry_Pi_1.GIPO5, R1.Pin_0
  N4: Raspberry_Pi_1.GIPO6, R2.Pin_0
  N5: Raspberry_Pi_1.GIPO13, J8.pin2
  N6: Raspberry_Pi_1.GIPO19, J8.pin1
  N7: J6.pin1, R1.Pin_1
  N8: J7.pin1, R2.Pin_1
